// Digital circuit lab03.dig as structural Verilog
module lab03 (
  input  [31:0] PC,
  input  [31:0] A,
  input  [31:0] B,
  output reg__dst,
  output branch,
  output mem__read,
  output mem__to__reg,
  output mem__write,
  output alu__src,
  output reg__write,
  output out_8,
  output [31:0] out_9
);

  wire [1:0] u_control_alu_op;
  wire [3:0] u_alu_control_alu_control;

  control #(.applicationType("IVERILOG"), .CodeFile("/workspaces/Lab03-DatapathControlUnit/control.v")) u_control (
    .instr_op(PC[31:26]), .reg_dst(reg__dst), .branch(branch), .mem_read(mem__read),
    .mem_to_reg(mem__to__reg), .alu_op(u_control_alu_op), .mem_write(mem__write), .alu_src(alu__src),
    .reg_write(reg__write));
  alu_control #(.applicationType("IVERILOG"), .CodeFile("/workspaces/Lab03-DatapathControlUnit/alu_control.v")) u_alu_control (
    .alu_op(u_control_alu_op), .funct(PC[5:0]), .alu_control(u_alu_control_alu_control));
  alu #(.applicationType("IVERILOG"), .CodeFile("/workspaces/Lab03-DatapathControlUnit/alu.v")) u_alu (
    .alu_control(u_alu_control_alu_control), .A(A), .B(B), .zero(out_8), .result(out_9));

  // Other names for the same wires on the sheet: instr__5__0[5:0] = PC[5:0]
endmodule
